// Logisim project cpu.circ as structural Verilog
module half_adder (
  input  a,
  input  b,
  output sum,
  output carry
);

  xor xor_1 (sum, a, b);
  and and_1 (carry, b, a);
endmodule

module full_adder (
  input  a,
  input  b,
  input  carry_in,
  output sum,
  output carry_out
);

  wire half_adder_1_carry, half_adder_1_sum, half_adder_2_carry;

  half_adder half_adder_1 (.a(a), .b(b), .sum(half_adder_1_sum), .carry(half_adder_1_carry));
  half_adder half_adder_2 (.a(half_adder_1_sum), .b(carry_in), .sum(sum), .carry(half_adder_2_carry));
  or or_1 (carry_out, half_adder_2_carry, half_adder_1_carry);
endmodule

module byte_adder (
  input  carry_in,
  input  a_0,
  input  a_1,
  input  a_2,
  input  a_3,
  input  a_4,
  input  a_5,
  input  a_6,
  input  a_7,
  input  b_0,
  input  b_1,
  input  b_2,
  input  b_3,
  input  b_4,
  input  b_5,
  input  b_6,
  input  b_7,
  output sum_0,
  output sum_1,
  output sum_2,
  output sum_3,
  output sum_4,
  output sum_5,
  output sum_6,
  output sum_7,
  output carry_out
);

  wire nibble_adder_1_carry_out;

  nibble_adder nibble_adder_1 (
    .carry(carry_in), .a_0(a_0), .a_1(a_1), .a_2(a_2), .a_3(a_3), .b_0(b_0), .b_1(b_1), .b_2(b_2), .b_3(b_3),
    .sum_0(sum_0), .sum_1(sum_1), .sum_2(sum_2), .sum_3(sum_3), .carry_out(nibble_adder_1_carry_out));
  nibble_adder nibble_adder_2 (
    .carry(nibble_adder_1_carry_out), .a_0(a_4), .a_1(a_5), .a_2(a_6), .a_3(a_7), .b_0(b_4), .b_1(b_5),
    .b_2(b_6), .b_3(b_7), .sum_0(sum_4), .sum_1(sum_5), .sum_2(sum_6), .sum_3(sum_7), .carry_out(carry_out));
endmodule

module nibble_adder (
  input  carry,
  input  a_0,
  input  a_1,
  input  a_2,
  input  a_3,
  input  b_0,
  input  b_1,
  input  b_2,
  input  b_3,
  output sum_0,
  output sum_1,
  output sum_2,
  output sum_3,
  output carry_out
);

  wire full_adder_1_carry_out, full_adder_2_carry_out, full_adder_3_carry_out;

  full_adder full_adder_1 (.a(a_0), .b(b_0), .carry_in(carry), .sum(sum_0), .carry_out(full_adder_1_carry_out));
  full_adder full_adder_2 (
    .a(a_1), .b(b_1), .carry_in(full_adder_1_carry_out), .sum(sum_1), .carry_out(full_adder_2_carry_out));
  full_adder full_adder_3 (
    .a(a_2), .b(b_2), .carry_in(full_adder_2_carry_out), .sum(sum_2), .carry_out(full_adder_3_carry_out));
  full_adder full_adder_4 (.a(a_3), .b(b_3), .carry_in(full_adder_3_carry_out), .sum(sum_3), .carry_out(carry_out));
endmodule

module word_adder (
  input  carry_in,
  input  a_0,
  input  a_1,
  input  a_2,
  input  a_3,
  input  a_4,
  input  a_5,
  input  a_6,
  input  a_7,
  input  a_8,
  input  a_9,
  input  a_10,
  input  a_11,
  input  a_12,
  input  a_13,
  input  a_14,
  input  a_15,
  input  b_0,
  input  b_1,
  input  b_2,
  input  b_3,
  input  b_4,
  input  b_5,
  input  b_6,
  input  b_7,
  input  b_8,
  input  b_9,
  input  b_10,
  input  b_11,
  input  b_12,
  input  b_13,
  input  b_14,
  input  b_15,
  output sum_0,
  output sum_1,
  output sum_2,
  output sum_3,
  output sum_4,
  output sum_5,
  output sum_6,
  output sum_7,
  output sum_8,
  output sum_9,
  output sum_10,
  output sum_11,
  output sum_12,
  output sum_13,
  output sum_14,
  output sum_15,
  output carry_out
);

  wire byte_adder_1_carry_out;

  byte_adder byte_adder_1 (
    .carry_in(carry_in), .a_0(a_0), .a_1(a_1), .a_2(a_2), .a_3(a_3), .a_4(a_4), .a_5(a_5), .a_6(a_6),
    .a_7(a_7), .b_0(b_0), .b_1(b_1), .b_2(b_2), .b_3(b_3), .b_4(b_4), .b_5(b_5), .b_6(b_6), .b_7(b_7),
    .sum_0(sum_0), .sum_1(sum_1), .sum_2(sum_2), .sum_3(sum_3), .sum_4(sum_4), .sum_5(sum_5), .sum_6(sum_6),
    .sum_7(sum_7), .carry_out(byte_adder_1_carry_out));
  byte_adder byte_adder_2 (
    .carry_in(byte_adder_1_carry_out), .a_0(a_8), .a_1(a_9), .a_2(a_10), .a_3(a_11), .a_4(a_12), .a_5(a_13),
    .a_6(a_14), .a_7(a_15), .b_0(b_8), .b_1(b_9), .b_2(b_10), .b_3(b_11), .b_4(b_12), .b_5(b_13), .b_6(b_14),
    .b_7(b_15), .sum_0(sum_8), .sum_1(sum_9), .sum_2(sum_10), .sum_3(sum_11), .sum_4(sum_12), .sum_5(sum_13),
    .sum_6(sum_14), .sum_7(sum_15), .carry_out(carry_out));
endmodule
